# Fritzing sketch Simdisplay (saved by Fritzing 0.9.4)
breadboards: 2

parts:
  Part1 = Arduino Uno (Rev3)
  U1 = 74HC595 [package="DIP16 [THT]"]
  U2 = 74HC595 [package="DIP16 [THT]"]
  R1 = Resistor [tolerance=±5% resistance=500 package="0603 [SMD]"]
  R2 = Resistor [tolerance=±5% resistance=500 package="0603 [SMD]"]
  R3 = Resistor [tolerance=±5% resistance=500 package="0603 [SMD]"]
  R4 = Resistor [tolerance=±5% resistance=500 package="0603 [SMD]"]
  R5 = Resistor [tolerance=±5% resistance=500 package="0603 [SMD]"]
  R6 = Resistor [tolerance=±5% resistance=500 package="0603 [SMD]"]
  R7 = Resistor [tolerance=±5% resistance=500 package="0603 [SMD]"]
  R8 = Resistor [tolerance=±5% resistance=500 package="0603 [SMD]"]
  U3 = 7-SEGMENT-DISPLAY [part_number=5161A6-1 package=7-segment-display]
  R9 = Resistor [tolerance=±5% resistance=10k package="0603 [SMD]"]
  R10 = Resistor [tolerance=±5% resistance=10k package="0603 [SMD]"]
  R11 = Resistor [tolerance=±5% resistance=5k package="0603 [SMD]"]
  R12 = Resistor [tolerance=±5% resistance=10k package="0603 [SMD]"]
  R13 = Resistor [tolerance=±5% resistance=5k package="0603 [SMD]"]
  R14 = Resistor [tolerance=±5% resistance=5k package="0603 [SMD]"]
  R15 = Resistor [tolerance=±5% resistance=1k package="0603 [SMD]"]
  R16 = Resistor [tolerance=±5% resistance=1k package="0603 [SMD]"]
  LED3 = smd LED [color="Yellow (595nm)" package="1206 [SMD]"]
  LED2 = smd LED [color="Red (635nm)" package="1206 [SMD]"]
  LED4 = smd LED [color="Yellow (595nm)" package="1206 [SMD]"]
  LED5 = smd LED [color="Yellow (595nm)" package="1206 [SMD]"]
  LED6 = smd LED [color="Green (555nm)" package="1206 [SMD]"]
  LED7 = smd LED [color="Green (555nm)" package="1206 [SMD]"]
  LED8 = smd LED [color="Green (555nm)" package="1206 [SMD]"]
  LCD1 = LCD screen
  R17 = Rotary Potentiometer (Small) [maximum_resistance=10kΩ package=THT]
  R18 = Resistor [tolerance=±5% resistance=100k package=THT]
  LED1 = smd LED [color="Red (635nm)" package="0805 [SMD]"]  # not connected

nets:
  N1: Part1.A0, LCD1.DB4
  N2: Part1.A1, LCD1.DB5
  N3: Part1.A2, LCD1.DB6
  N4: Part1.A3, LCD1.DB7
  N5: Part1.A4/SDA, LCD1.RS
  N6: Part1.A5/SCL, LCD1.E
  N7: Part1.D2, U1.ST_CP
  N8: Part1.D3_PWM, U2.ST_CP
  N9: Part1.D5_PWM, U1.SH_CP, U2.SH_CP
  N10: Part1.D6_PWM, U1.DS, U2.DS
  VCC: Part1.5V, U1.MR, U1.VCC, U2.MR, U2.VCC, LCD1.VDD, LCD1.LED+, R17.leg2
  GND: Part1.GND, U1.GND, U1.OE, U2.GND, U2.OE, U3.C, U3.F, R9.Pin_0, R10.Pin_0, R11.Pin_0, R12.Pin_0, R13.Pin_0, R14.Pin_0, R15.Pin_0, R16.Pin_0, LCD1.VSS, LCD1.R/W, R17.leg1, R18.Pin_1
  N11: U1.Q1, LED2.anode
  N12: U1.Q2, LED3.anode
  N13: U1.Q3, LED4.anode
  N14: U1.Q4, LED5.anode
  N15: U1.Q5, LED6.anode
  N16: U1.Q6, LED7.anode
  N17: U1.Q7, LED8.anode
  N18: U2.Q1, R2.Pin_1
  N19: U2.Q2, R1.Pin_1
  N20: U2.Q3, R4.Pin_1
  N21: U2.Q4, R5.Pin_1
  N22: U2.Q5, R6.Pin_1
  N23: U2.Q6, R7.Pin_1
  N24: U2.Q7, R8.Pin_1
  N25: U2.Q0, R3.Pin_1
  N26: R1.Pin_0, U3.D
  N27: R2.Pin_0, U3.G
  N28: R3.Pin_0, U3.B
  N29: R4.Pin_0, U3.G1
  N30: R5.Pin_0, U3.DP
  N31: R6.Pin_0, U3.A
  N32: R7.Pin_0, U3.G2
  N33: R8.Pin_0, U3.E
  N34: R9.Pin_1, LED8.cathode
  N35: R10.Pin_1, LED7.cathode
  N36: R11.Pin_1, LED5.cathode
  N37: R12.Pin_1, LED6.cathode
  N38: R13.Pin_1, LED4.cathode
  N39: R14.Pin_1, LED3.cathode
  N40: R15.Pin_1, LED2.cathode
  N41: LCD1.V0, R17.wiper
  N42: LCD1.LED-, R18.Pin_0
